# Fritzing sketch cheshire-clock (saved by Fritzing 0.9.0b)
breadboards: 1

parts:
  Part1 = Arduino Uno (Rev3)
  hour_circle = Neopixel Ring 12
  RTC1 = DS1307 RTC Breakout
  hour_quarter_(actually_a_15LED_stick) = Neopixel Ring 12
  minute_quarter_(15_LED_stick) = Neopixel Ring 12

nets:
  N1: Part1.A4/SDA, RTC1.SCL
  N2: Part1.A5/SCL, RTC1.SDA
  N3: Part1.D4, minute_quarter_(15_LED_stick).IN
  N4: Part1.D5_PWM, hour_quarter_(actually_a_15LED_stick).IN
  N5: Part1.D6_PWM, hour_circle.IN
  VCC: Part1.5V, hour_circle.VCC, RTC1.5V, hour_quarter_(actually_a_15LED_stick).VCC, minute_quarter_(15_LED_stick).VCC
  GND: Part1.GND, hour_circle.GND, RTC1.GND

custom parts:
  Neopixel Ring 12: Neopixel Ring x12
  DS1307 RTC Breakout: DS1307 Real-time Clock Breakout Board with Battery
